// Logisim project DE Assignment.circ as structural Verilog: 1 circuit, main circuit main
module main (
  input  in_1,
  input  TURN_ON_ALL,
  input  in_3,
  input  SELECTED_PC,
  input  _6,
  input  _5,
  input  _4,
  input  _3,
  input  _2,
  input  _1,
  input  in_11,
  input  in_12,
  output [3:0] out_13,
  output [2:0] out_14
);

  wire and_1_out, and_2_out, and_3_out, and_4_out, and_5_out, and_6_out, and_7_out, and_8_out, and_9_out,
       and_10_out, and_11_out, and_12_out, and_13_out, and_14_out, and_15_out, and_16_out, and_17_out,
       button_1_out, clock_1_out, d_ff_1_q, d_ff_2_q, d_ff_3_q, d_ff_4_q, d_ff_5_q, d_ff_6_q, d_ff_7_q,
       d_ff_8_q, d_ff_9_q, d_ff_10_q, decoder_1_out0, decoder_1_out1, decoder_1_out2, decoder_1_out3,
       decoder_1_out4, decoder_1_out5, decoder_1_out6, decoder_1_out7, or_1_out, or_2_out, or_3_out,
       or_4_out, or_5_out, or_6_out, xnor_1_out, xnor_2_out, xnor_3_out, xnor_4_out, xnor_5_out;

  D_Flip_Flop d_ff_1 (.clk(clock_1_out), .D(in_1), .Q(d_ff_1_q));  // open: Qn, preset, en, reset
  D_Flip_Flop d_ff_2 (.clk(clock_1_out), .D(in_3), .Q(d_ff_2_q));  // open: Qn, preset, en, reset
  D_Flip_Flop d_ff_3 (.clk(clock_1_out), .D(in_11), .Q(d_ff_3_q));  // open: Qn, preset, en, reset
  D_Flip_Flop d_ff_4 (.clk(clock_1_out), .D(in_12), .Q(d_ff_4_q));  // open: Qn, preset, en, reset
  Clock clock_1 (.out(clock_1_out));
  xnor xnor_1 (xnor_1_out, d_ff_1_q, 1'b0);
  xnor xnor_2 (xnor_2_out, d_ff_2_q, 1'b1);
  xnor xnor_3 (xnor_3_out, d_ff_3_q, 1'b1);
  xnor xnor_4 (xnor_4_out, d_ff_4_q, 1'b0);
  and and_1 (and_1_out, xnor_1_out, xnor_2_out, xnor_3_out, xnor_4_out);
  and and_2 (and_2_out, SELECTED_PC, and_1_out);
  and and_3 (and_3_out, and_1_out, 1'b1);
  and and_4 (and_4_out, TURN_ON_ALL, decoder_1_out1, and_1_out);
  and and_5 (and_5_out, TURN_ON_ALL, TURN_ON_ALL);
  xnor xnor_5 (xnor_5_out, TURN_ON_ALL, TURN_ON_ALL);
  Priority_Encoder priority_encoder_1 (
    .in0(xnor_5_out), .in1(and_5_out), .in2(and_11_out), .in3(and_10_out), .in4(and_8_out), .in5(and_9_out),
    .in6(and_6_out), .in7(and_7_out), .out(out_14));  // open: en_in, gs, en_out
  Decoder #(.select(3)) decoder_1 (
    .out0(decoder_1_out0), .out1(decoder_1_out1), .out2(decoder_1_out2), .out3(decoder_1_out3),
    .out4(decoder_1_out4), .out5(decoder_1_out5), .out6(decoder_1_out6), .out7(decoder_1_out7), .sel(out_14));  // open: en
  and and_6 (and_6_out, and_2_out, _5);
  and and_7 (and_7_out, and_2_out, _6);
  and and_8 (and_8_out, and_2_out, _3);
  and and_9 (and_9_out, and_2_out, _4);
  and and_10 (and_10_out, and_2_out, _2);
  and and_11 (and_11_out, and_2_out, _1);
  or or_1 (or_1_out, and_4_out, ~and_3_out, and_11_out, decoder_1_out2);  // OR_Gate
  or or_2 (or_2_out, and_4_out, ~and_3_out, and_10_out, decoder_1_out3);  // OR_Gate
  or or_3 (or_3_out, and_4_out, ~and_3_out, and_8_out, decoder_1_out4);  // OR_Gate
  or or_4 (or_4_out, and_4_out, ~and_3_out, and_9_out, decoder_1_out5);  // OR_Gate
  or or_5 (or_5_out, and_4_out, ~and_3_out, and_6_out, decoder_1_out6);  // OR_Gate
  or or_6 (or_6_out, and_4_out, ~and_3_out, and_7_out, decoder_1_out7);  // OR_Gate
  D_Flip_Flop d_ff_5 (.clk(clock_1_out), .D(or_1_out), .Q(d_ff_5_q));  // open: Qn, preset, en, reset
  D_Flip_Flop d_ff_6 (.clk(clock_1_out), .D(or_2_out), .Q(d_ff_6_q));  // open: Qn, preset, en, reset
  D_Flip_Flop d_ff_7 (.clk(clock_1_out), .D(or_3_out), .Q(d_ff_7_q));  // open: Qn, preset, en, reset
  D_Flip_Flop d_ff_8 (.clk(clock_1_out), .D(or_4_out), .Q(d_ff_8_q));  // open: Qn, preset, en, reset
  D_Flip_Flop d_ff_9 (.clk(clock_1_out), .D(or_5_out), .Q(d_ff_9_q));  // open: Qn, preset, en, reset
  D_Flip_Flop d_ff_10 (.clk(clock_1_out), .D(or_6_out), .Q(d_ff_10_q));  // open: Qn, preset, en, reset
  Button button_1 (.out(button_1_out));
  and and_12 (and_12_out, clock_1_out, d_ff_5_q);
  and and_13 (and_13_out, clock_1_out, d_ff_6_q);
  and and_14 (and_14_out, clock_1_out, d_ff_7_q);
  and and_15 (and_15_out, clock_1_out, d_ff_8_q);
  and and_16 (and_16_out, clock_1_out, d_ff_9_q);
  and and_17 (and_17_out, clock_1_out, d_ff_10_q);
  LED led_1 (.in(d_ff_5_q));
  LED led_2 (.in(d_ff_6_q));
  LED led_3 (.in(d_ff_7_q));
  LED led_4 (.in(d_ff_8_q));
  LED led_5 (.in(d_ff_9_q));
  LED led_6 (.in(d_ff_10_q));
  Counter counter_1 (.clk(and_12_out), .clr(button_1_out));  // open: load, D, count, Q, carry
  Counter counter_2 (.clk(and_13_out), .clr(button_1_out));  // open: load, D, count, Q, carry
  Counter counter_3 (.clk(and_14_out), .clr(button_1_out));  // open: load, D, count, Q, carry
  Counter counter_4 (.clk(and_15_out), .clr(button_1_out));  // open: load, D, count, Q, carry
  Counter counter_5 (.clk(and_16_out), .clr(button_1_out));  // open: load, D, count, Q, carry
  Counter counter_6 (.clk(and_17_out), .clr(button_1_out));  // open: load, D, count, Q, carry

  assign out_13 = 4'b0110;

  // Notes on the sheet:
  //   PLEASE ENTER KEY
  //   set password (0110)
  //   PRIORITT 1
  //   PRIORITY 2
  //   COMPUTER LAB ADMIN CONTROL SYSTEM
  //   RESET
  //   1
  //   2
  //   3
  //   4
  //   5
  //   6
endmodule
